# Fritzing sketch circspeedcontr (saved by Fritzing 0.9.3b)
breadboards: 1

parts:
  R1 = Resistor [tolerance=±5% resistance=220 package=THT]
  R2 = Resistor [tolerance=±5% resistance=10k package=THT]
  Q1 = TRANSISTOR_NPN [part_number=BD243C package=to-92-ammo]
  V1 = DC Power [voltage=12V]
  Raspberry_Pi_1 = Raspberry Pi 3 [part_number=RPI-3-V1.2]
  M1 = DC Motor
  U4 = MCP41xxx [part_number=MCP4131 package=so08]

nets:
  N1: R1.Pin_0, U4.A
  N2: R1.Pin_1, Q1.C, V1.V+
  GND: R2.Pin_0, V1.V-, Raspberry_Pi_1.GND, M1.pin_2, U4.GND
  N3: R2.Pin_1, U4.B
  N4: Q1.E, M1.pin_1
  N5: Q1.B, U4.W
  3V3: Raspberry_Pi_1.3V3, U4.VCC
  N6: Raspberry_Pi_1.GPIO10, U4.DI
  N7: Raspberry_Pi_1.GPIO11, U4.SCK
  N8: Raspberry_Pi_1.GPIO8, U4.CS
