# Fritzing sketch circspeeddet (saved by Fritzing 0.9.3b)
breadboards: 1

parts:
  Raspberry_Pi_1 = Raspberry Pi 3 [part_number=RPI-3-V1.2]
  U2 = HALL-EFFECT [part_number=US5881 package=sc70]

nets:
  GND: Raspberry_Pi_1.GND, U2.GND
  N1: Raspberry_Pi_1.GPIO23, U2.OUT
  5V: Raspberry_Pi_1.5V, U2.VCC

custom parts:
  HALL-EFFECT: Hall effect sensor in SC70 package
